# Fritzing sketch Bidireccional Com. Arduino - ESP01 (saved by Fritzing 0.9.3b)
circuit board: 8.46667cm x 5.64444cm
breadboards: 1

parts:
  U1 = ESP8266 WiFi Module [part_number=ESP8266]
  Componente1 = Arduino Uno (Rev3)
  S1 = Pushbutton [package="[THT]"]

nets:
  VCC: U1.VCC, U1.CH_PD, Componente1.3V3
  N1: U1.GPIO_0, Componente1.D7
  N2: U1.GPIO_2, Componente1.D8
  GND: U1.GND, Componente1.GND, S1.Pin_1, S1.Pin_2
  N3: Componente1.D2, S1.Pin_3, S1.Pin_4

custom parts:
  ESP8266 WiFi Module: Generic WiFi Module based on the ESP8266 with onboard PCB antenna and UART communications
